# Fritzing sketch IRLock_Sketch (saved by Fritzing 0.9.3b)
breadboards: 1

parts:
  Componente1 = Arduino Uno (Rev3)
  LCD1 = LCD screen
  R1 = Rotary Potentiometer (Small) [maximum_resistance=100kΩ package=THT]
  IR1 = TSOP312.., 314.. [package=THT]
  J1 = Piezo Speaker
  J3 = Basic Servo

nets:
  N1: Componente1.D9_PWM, J3.pulse
  N2: Componente1.D11_PWM/MOSI, LCD1.E
  N3: Componente1.D12/MISO, LCD1.RS
  GND: Componente1.GND, LCD1.VSS, LCD1.R/W, LCD1.LED-, R1.leg1, IR1.GND, J1.pin1, J3.gnd
  N4: Componente1.D2, LCD1.DB7
  N5: Componente1.D3_PWM, LCD1.DB6
  N6: Componente1.D4, LCD1.DB5
  N7: Componente1.D5_PWM, LCD1.DB4
  N8: Componente1.D6_PWM, J1.pin2
  N9: Componente1.D7, IR1.Data
  5V: Componente1.5V, LCD1.VDD, LCD1.LED+, R1.leg2, IR1.Vs, J3.vcc
  N10: LCD1.V0, R1.wiper
